# Fritzing sketch Bluetooth_4WD_Robot (saved by Fritzing 0.9.5d)

parts:
  Main_Controller_(STM32_Blue_Pill_Board_-_Powered_by_5V_USB_Power_Bank) = STM32F103C8T6 blue mini board
  Motor_Power_Switch_(SPST_-_Controls_6V_Battery_to_Motors) = SWITCH-SPST-2 [package=switch-spst-vertical]
  Motor_Driver_(L298N_Dual_H-Bridge) = L298_BRIDGE_DRIVER [package=powerso20]
  Bluetooth_Module_(HC-05_-_Powered_from_Blue_Pill_3_3V_Rail) = Bluetooth HC-05 Macho
  Obstacle_Detection_Sensor_(HC-SR04_-_Powered_from_5V_Rail) = hc-sr04
  R_ECHO_TOP_-_2_2k_(Echo_Protection_Divider) = Resistor [resistance=2200 tolerance=±5% package=THT]
  R_ECHO_BOT_-_4_7k_(Echo_Protection_Divider) = Resistor [resistance=4700 tolerance=±5% package=THT]
  AA_Battery_1_(Motor_Pack) = Battery Holders [package=battery-aa]
  AA_Battery_2_(Motor_Pack) = Battery Holders [package=battery-aa]
  AA_Battery_3_(Motor_Pack) = Battery Holders [package=battery-aa]
  AA_Battery_4_(6V_Motor_Pack) = Battery Holders [package=battery-aa]
  Front_Left_Motor_(FL) = DC Motor
  Rear_Left_Motor_(RL) = DC Motor
  Front_Right_Motor_(FR) = DC Motor
  Rear_Right_Motor_(RR) = DC Motor
  R1_-_220_Ohm_(Green_Status_LED) = Resistor [resistance=220 tolerance=±5% package=THT]
  Green_LED_-_Power_Indicator_(Front) = LED - 5mm [color=green package="5 mm [THT]"]
  R2_-_220_Ohm_(Blue_Status_LED) = Resistor [resistance=220 tolerance=±5% package=THT]
  Blue_LED_-_Bluetooth_Connected_(Front) = LED - 5mm [color=blue package="5 mm [THT]"]
  R3_-_220_Ohm_(Brake_LED_1) = Resistor [resistance=220 tolerance=±5% package=THT]
  Brake_Light_1_-_Outer_Left_(Rear) = LED - 5mm [color=red package="5 mm [THT]"]
  R5_-_220_Ohm_(Brake_LED_3) = Resistor [resistance=220 tolerance=±5% package=THT]
  Brake_Light_3_-_Inner_Left_(Rear) = LED - 5mm [color=red package="5 mm [THT]"]
  R6_-_220_Ohm_(Brake_LED_4) = Resistor [resistance=220 tolerance=±5% package=THT]
  Brake_Light_4_-_Inner_Right_(Rear) = LED - 5mm [color=red package="5 mm [THT]"]
  R4_-_220_Ohm_(Brake_LED_2) = Resistor [resistance=220 tolerance=±5% package=THT]
  Brake_Light_2_-_Outer_Right_(Rear) = LED - 5mm [color=red package="5 mm [THT]"]

nets:
  N1: Main_Controller_(STM32_Blue_Pill_Board_-_Powered_by_5V_USB_Power_Bank).B12, Bluetooth_Module_(HC-05_-_Powered_from_Blue_Pill_3_3V_Rail).Key
  N2: Main_Controller_(STM32_Blue_Pill_Board_-_Powered_by_5V_USB_Power_Bank).A9, Bluetooth_Module_(HC-05_-_Powered_from_Blue_Pill_3_3V_Rail).RXD
  N3: Main_Controller_(STM32_Blue_Pill_Board_-_Powered_by_5V_USB_Power_Bank).A10, Bluetooth_Module_(HC-05_-_Powered_from_Blue_Pill_3_3V_Rail).TXD
  N4: Main_Controller_(STM32_Blue_Pill_Board_-_Powered_by_5V_USB_Power_Bank).B5, R1_-_220_Ohm_(Green_Status_LED).Pin_0
  N5: Main_Controller_(STM32_Blue_Pill_Board_-_Powered_by_5V_USB_Power_Bank).B6, R2_-_220_Ohm_(Blue_Status_LED).Pin_0
  N6: Main_Controller_(STM32_Blue_Pill_Board_-_Powered_by_5V_USB_Power_Bank).B7, R3_-_220_Ohm_(Brake_LED_1).Pin_0, R5_-_220_Ohm_(Brake_LED_3).Pin_0
  N7: Main_Controller_(STM32_Blue_Pill_Board_-_Powered_by_5V_USB_Power_Bank).B8, R6_-_220_Ohm_(Brake_LED_4).Pin_0, R4_-_220_Ohm_(Brake_LED_2).Pin_0
  5V: Main_Controller_(STM32_Blue_Pill_Board_-_Powered_by_5V_USB_Power_Bank).5V, Motor_Driver_(L298N_Dual_H-Bridge).VSS, Obstacle_Detection_Sensor_(HC-SR04_-_Powered_from_5V_Rail).VCC
  GND: Main_Controller_(STM32_Blue_Pill_Board_-_Powered_by_5V_USB_Power_Bank).G, Motor_Driver_(L298N_Dual_H-Bridge).GND, Bluetooth_Module_(HC-05_-_Powered_from_Blue_Pill_3_3V_Rail).GND, Obstacle_Detection_Sensor_(HC-SR04_-_Powered_from_5V_Rail).GND, R_ECHO_BOT_-_4_7k_(Echo_Protection_Divider).Pin_1, AA_Battery_1_(Motor_Pack).-, Green_LED_-_Power_Indicator_(Front).cathode, Blue_LED_-_Bluetooth_Connected_(Front).cathode, Brake_Light_1_-_Outer_Left_(Rear).cathode, Brake_Light_3_-_Inner_Left_(Rear).cathode, Brake_Light_4_-_Inner_Right_(Rear).cathode, Brake_Light_2_-_Outer_Right_(Rear).cathode
  3.3V: Main_Controller_(STM32_Blue_Pill_Board_-_Powered_by_5V_USB_Power_Bank).3.3V, Bluetooth_Module_(HC-05_-_Powered_from_Blue_Pill_3_3V_Rail).VCC
  N8: Main_Controller_(STM32_Blue_Pill_Board_-_Powered_by_5V_USB_Power_Bank).A0, Motor_Driver_(L298N_Dual_H-Bridge).IN1
  N9: Main_Controller_(STM32_Blue_Pill_Board_-_Powered_by_5V_USB_Power_Bank).A1, Motor_Driver_(L298N_Dual_H-Bridge).IN2
  N10: Main_Controller_(STM32_Blue_Pill_Board_-_Powered_by_5V_USB_Power_Bank).A2, Motor_Driver_(L298N_Dual_H-Bridge).IN3
  N11: Main_Controller_(STM32_Blue_Pill_Board_-_Powered_by_5V_USB_Power_Bank).A3, Motor_Driver_(L298N_Dual_H-Bridge).IN4
  N12: Main_Controller_(STM32_Blue_Pill_Board_-_Powered_by_5V_USB_Power_Bank).A6, Motor_Driver_(L298N_Dual_H-Bridge).ENA
  N13: Main_Controller_(STM32_Blue_Pill_Board_-_Powered_by_5V_USB_Power_Bank).A7, Motor_Driver_(L298N_Dual_H-Bridge).ENB
  N14: Main_Controller_(STM32_Blue_Pill_Board_-_Powered_by_5V_USB_Power_Bank).B0, Obstacle_Detection_Sensor_(HC-SR04_-_Powered_from_5V_Rail).Trig
  N15: Main_Controller_(STM32_Blue_Pill_Board_-_Powered_by_5V_USB_Power_Bank).B1, R_ECHO_TOP_-_2_2k_(Echo_Protection_Divider).Pin_1, R_ECHO_BOT_-_4_7k_(Echo_Protection_Divider).Pin_0
  N16: Motor_Power_Switch_(SPST_-_Controls_6V_Battery_to_Motors).O, Motor_Driver_(L298N_Dual_H-Bridge).VS
  N17: Motor_Power_Switch_(SPST_-_Controls_6V_Battery_to_Motors).P, AA_Battery_4_(6V_Motor_Pack).+
  N18: Motor_Driver_(L298N_Dual_H-Bridge).OUT1, Front_Left_Motor_(FL).pin_1, Rear_Left_Motor_(RL).pin_1
  N19: Motor_Driver_(L298N_Dual_H-Bridge).OUT2, Front_Left_Motor_(FL).pin_2, Rear_Left_Motor_(RL).pin_2
  N20: Motor_Driver_(L298N_Dual_H-Bridge).OUT3, Front_Right_Motor_(FR).pin_1, Rear_Right_Motor_(RR).pin_1
  N21: Motor_Driver_(L298N_Dual_H-Bridge).OUT4, Front_Right_Motor_(FR).pin_2, Rear_Right_Motor_(RR).pin_2
  N22: Obstacle_Detection_Sensor_(HC-SR04_-_Powered_from_5V_Rail).Echo, R_ECHO_TOP_-_2_2k_(Echo_Protection_Divider).Pin_0
  N23: AA_Battery_1_(Motor_Pack).+, AA_Battery_2_(Motor_Pack).-
  N24: AA_Battery_2_(Motor_Pack).+, AA_Battery_3_(Motor_Pack).-
  N25: AA_Battery_3_(Motor_Pack).+, AA_Battery_4_(6V_Motor_Pack).-
  N26: R1_-_220_Ohm_(Green_Status_LED).Pin_1, Green_LED_-_Power_Indicator_(Front).anode
  N27: R2_-_220_Ohm_(Blue_Status_LED).Pin_1, Blue_LED_-_Bluetooth_Connected_(Front).anode
  N28: R3_-_220_Ohm_(Brake_LED_1).Pin_1, Brake_Light_1_-_Outer_Left_(Rear).anode
  N29: R5_-_220_Ohm_(Brake_LED_3).Pin_1, Brake_Light_3_-_Inner_Left_(Rear).anode
  N30: R6_-_220_Ohm_(Brake_LED_4).Pin_1, Brake_Light_4_-_Inner_Right_(Rear).anode
  N31: R4_-_220_Ohm_(Brake_LED_2).Pin_1, Brake_Light_2_-_Outer_Right_(Rear).anode
